# Fritzing sketch linked_lines_dual_powers_simple (saved by Fritzing 0.9.5d)
# 18650 Li-ion Battery: CC-BY Dr Kristofer Chan, King's College London/Remote-research.org
circuit board: 8.46667cm x 5.64444cm
stripboards: 1

parts:
  J11 = Screw terminal - 2 pins [package=THT]
  J12 = Screw terminal - 2 pins [package=THT]
  元件1 = Motor Driver 1A Dual TB6612FNG
  M1 = DC Motor
  M2 = DC Motor
  J21 = female pin header, 4 pins [form="♀ (female)"]
  J23 = Screw terminal - 2 pins [package=THT]
  J24 = female pin header, 4 pins [form="♀ (female)"]
  S2 = Toggle Switch [package=THT]
  U2 = MAX323 [package=so08]
  J25 = Basic Servo
  J26 = Basic Servo
  J3 = female pin header, 5 pins [form="♀ (female)"]
  Raspberry_Pi_1 = Raspberry Pi 3 [part_number=RPI-3-V1.2]
  M3 = RioRand LM2596
  U3 = TRANSCHIPTC5747 [package=camera_sfv24r-2st_2]  # not connected
  J20 = male pin header, 2 pins [form="♂ (male)"]
  J27 = female pin header, 4 pins [form="♀ (female)"]
  J28 = female pin header, 4 pins [form="♀ (female)"]
  BAT1 = 18650 Li-ion Battery [package=battery-18650]
  BAT2 = 18650 Li-ion Battery [package=battery-18650]
  BAT3 = 18650 Li-ion Battery [package=battery-18650]
  BAT4 = 18650 Li-ion Battery [package=battery-18650]
  LED1 = LED - 5mm [color="Red (633nm)" package="5 mm [THT]"]
  R1 = Resistor [tolerance=±5% resistance=680 package=THT]

nets:
  N1: J11.pin1, M1.pin_2, Raspberry_Pi_1.GPIO4
  N2: J11.pin2, M1.pin_1
  N3: J12.pin1, M2.pin_2
  N4: J12.pin2, M2.pin_1
  N5: 元件1.A02, 元件1.A01
  N6: 元件1.AIN2, J3.pin5
  N7: 元件1.AIN1, J3.pin4, Raspberry_Pi_1.GPIO5
  3V3: 元件1.STBY, J3.pin3, Raspberry_Pi_1.3v3, Raspberry_Pi_1.3V3
  N8: 元件1.BIN1, U2.NO1, U2.COM1, U2.IN2, U2.V-, J3.pin2, Raspberry_Pi_1.GPIO27
  N9: 元件1.BIN2, J3.pin1, Raspberry_Pi_1.GPIO17
  GND: J21.pin1, J24.pin1, J25.gnd, J26.gnd, Raspberry_Pi_1.GND, J20.pin2, J27.pin1, J27.pin2, J27.pin3, J27.pin4
  VCC: J21.pin2, J24.pin2, J25.vcc, J26.vcc, J20.pin1, J28.pin1, J28.pin2, J28.pin3, J28.pin4
  N10: J21.pin3, J24.pin3, J25.pulse, J26.pulse
  N11: J21.pin4, J24.pin4, Raspberry_Pi_1.GPIO19, Raspberry_Pi_1.GPIO18
  N12: J23.pin1, J23.pin2, BAT1.+, BAT2.-, R1.Pin_1
  N13: S2.L1, LED1.anode, R1.Pin_0
  N14: S2.COM, S2.L2
  N15: U2.NO2, U2.COM2, U2.IN1, U2.V+
  N16: M3.Pin_1, BAT3.+
  N17: M3.Pin_2, BAT4.-
  N18: BAT1.-, BAT2.+
  N19: BAT3.-, BAT4.+

custom parts:
  18650 Li-ion Battery: 18650 li-ion Battery Standard 18650 battery with interactive connectors Creative Common Attribution 4.0 International (CC-BY 4.0) license. Any use of this part requires attribution of Dr Kristofer Chan, Department of Geography, King's College London. Contact kristofer.chan [at] kcl.ac.uk OR kris [at] remote-research.org for further information.
